# Fritzing sketch PCBDesign (saved by Fritzing 0.9.3b)
circuit board: 6.78961cm x 5.92187cm
breadboards: 1

parts:
  Raspberry_Pi = double row male pin header, 10 pins [form="♂ (male)"]
  BerryGPS_IMU_v3 = double row male pin header, 10 pins [form="♂ (male)"]
  Heart_Rate = Pulse Sensor [package=SIP]
  ADS1015 = Adafruit ADS1015 12Bit I2C ADC [part_number="Adafruit #1083"]

nets (from the pcb view):
  VCC: Raspberry_Pi.pin1, BerryGPS_IMU_v3.pin1, Heart_Rate.Vcc, ADS1015.VDD
  N1: Raspberry_Pi.pin2, BerryGPS_IMU_v3.pin2, ADS1015.SDA
  N2: Raspberry_Pi.pin3, BerryGPS_IMU_v3.pin3, ADS1015.SCL
  N3: Raspberry_Pi.pin4, BerryGPS_IMU_v3.pin4
  N4: Raspberry_Pi.pin5, BerryGPS_IMU_v3.pin5
  N5: Raspberry_Pi.pin6, BerryGPS_IMU_v3.pin6
  N6: Raspberry_Pi.pin7, BerryGPS_IMU_v3.pin7
  GND: Raspberry_Pi.pin8, BerryGPS_IMU_v3.pin8, Heart_Rate.GND, ADS1015.GND
  N7: Raspberry_Pi.pin9, BerryGPS_IMU_v3.pin9
  N8: Raspberry_Pi.pin10, BerryGPS_IMU_v3.pin10
  N9: Heart_Rate.Signal, ADS1015.AIN0

notes:
  Raspberry Pi
  BerryGPS IMU v3
  Quyen Lu
  Kevin Lieng
  Seung Min

custom parts:
  Pulse Sensor: Pulse Sensor Optical Heart Rate Monitor for Arduino and other microcontrollers
  Adafruit ADS1015 12Bit I2C ADC: For microcontrollers without an analog-to-digital converter or when you want a higher-precision ADC, the ADS1015 provides 12-bit precision at 3300 samples/second over I2C. The chip can be configured as 4 single-ended input channels, or two differential channels. As a nice bonus, it even includes a programmable gain amplifier, up to x16, to help boost up smaller single/differential signals to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
